# Fritzing sketch coffee-roasting (saved by Fritzing 0.9.3b)
breadboards: 1

parts:
  Raspberry_Pi_1 = Raspberry Pi 3 [part_number=RPI-3-V1.2]
  Part1 = Adafruit MAX31865 RTD Sensor Breakout [part_number="Adafruit #3328"]

nets:
  3V3: Raspberry_Pi_1.3v3, Part1.VIN
  N1: Raspberry_Pi_1.GPIO22, Part1.SDO
  N2: Raspberry_Pi_1.GPIO21, Part1.CS
  N3: Raspberry_Pi_1.GPIO24, Part1.SCLK
  N4: Raspberry_Pi_1.GPIO23, Part1.SDI
  GND: Raspberry_Pi_1.GND, Part1.GND

notes:
  3-wire PT100

custom parts:
  Adafruit MAX31865 RTD Sensor Breakout: For precision temperature sensing, nothing beats a Platinum RTD. Resistance temperature detectors (RTDs) are temperature sensors that contain a resistor that changes resistance value as its temperature changes, basically a kind of thermistor. In this sensor, the resistor is actually a small strip of Platinum with a resistance of 100 ohms at 0°C, thus the name PT100. Compared to most NTC/PTC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
